# Fritzing sketch strollerAnalogMega (saved by Fritzing 0.9.10b)
circuit board: 10.1776cm x 5.36194cm

parts:
  Stroller_Pi_2_0 = Arduino Mega 2560 (Rev3)
  B_L = female pin header, 4 pins [form="♀ (female)"]
  B_R = female pin header, 4 pins [form="♀ (female)"]
  F = female pin header, 4 pins [form="♀ (female)"]
  F_R = female pin header, 4 pins [form="♀ (female)"]
  F_L = female pin header, 4 pins [form="♀ (female)"]
  I2C = female pin header, 4 pins [form="♀ (female)"]
  BRAKES = female pin header, 4 pins [form="♀ (female)"]

nets:
  N1: Stroller_Pi_2_0.A10, F_R.pin4
  N2: Stroller_Pi_2_0.A12, F.pin4
  N3: Stroller_Pi_2_0.A1, B_L.pin4
  N4: Stroller_Pi_2_0.A3, B_R.pin4
  N5: Stroller_Pi_2_0.A7, F_L.pin4
  N6: Stroller_Pi_2_0.D21/SCL, I2C.pin1
  N7: Stroller_Pi_2_0.D20/SDA, I2C.pin2
  N8: Stroller_Pi_2_0.GND, B_L.pin1, B_R.pin1, F.pin1, F_R.pin1, F_L.pin1, I2C.pin4, BRAKES.pin4
  N9: Stroller_Pi_2_0.D12_PWM, F_R.pin3
  N10: Stroller_Pi_2_0.D10_PWM, BRAKES.pin1
  N11: Stroller_Pi_2_0.D9_PWM, B_L.pin3
  N12: Stroller_Pi_2_0.D8_PWM, F.pin3
  N13: Stroller_Pi_2_0.5V, B_L.pin2, B_R.pin2, F.pin2, F_R.pin2, F_L.pin2, I2C.pin3, BRAKES.pin3
  N14: Stroller_Pi_2_0.D3_PWM, BRAKES.pin2
  N15: Stroller_Pi_2_0.D5_PWM, F_L.pin3
  N16: Stroller_Pi_2_0.D7_PWM, B_R.pin3

notes:
  mega shield
