# Fritzing sketch strollerRPI (saved by Fritzing 0.9.10b)
circuit board: 7.10869cm x 2.02776cm

parts:
  DS2 = DS18B20 1-Wire Temperature Sensor [part_number=DS18B20]
  I2C = female pin header, 3 pins [form="♀ (female)"]
  TEMP = female pin header, 3 pins [form="♀ (female)"]
  R2 = Resistor [tolerance=±5% resistance=4.7k power=0.25 package=THT]
  strollerRPI = Raspberry Pi 4B

nets:
  GND: DS2.GND, I2C.pin1, TEMP.pin3, strollerRPI.GND
  N1: DS2.DQ, TEMP.pin2, R2.Pin_1, strollerRPI.GPIO4
  VDD: DS2.VDD, TEMP.pin1, R2.Pin_0, strollerRPI.3V3
  N2: I2C.pin2, strollerRPI.GPIO3
  N3: I2C.pin3, strollerRPI.GPIO2

notes:
  Stroller Pi 2.0
  rpi shield
  i2c
